# Fritzing sketch Count Up Box Schematic (saved by Fritzing 0.8.5b)
circuit board: 9.5cm x 2.5cm
circuit board: 9.5cm x 2.5cm
breadboards: 2

parts:
  Batt_+ = female pin header, 1 pin [form="♀ (female)"]
  Batt_- = female pin header, 1 pin [form="♀ (female)"]
  -_for_LEDs = female pin header, 1 pin [form="♀ (female)"]
  R13 = Resistor [tolerance=±5% resistance=220 package=THT]
  R14 = Resistor [tolerance=±5% resistance=10k package=THT]
  R15 = Resistor [tolerance=±5% resistance=10k package=THT]
  IC4 = DS1307 [package=THT]
  Xtal = female pin header, 1 pin [form="♀ (female)"]
  32_kHz = female pin header, 1 pin [form="♀ (female)"]
  J12 = female pin header, 4 pins [form="♀ (female)"]

nets:
  N1: Batt_+.pin1, IC4.Vbat_-_Backup_Supply
  N2: Batt_-.pin1, R13.Pin_1, IC4.0V, J12.pin2
  N3: -_for_LEDs.pin1, R13.Pin_0
  N4: R14.Pin_0, R15.Pin_0, IC4.+V, J12.pin1
  N5: R14.Pin_1, IC4.SCL_-_I2C_Clock, J12.pin4
  N6: R15.Pin_1, IC4.SDA_-_I2C_Data, J12.pin3
  N7: IC4.X1_-_Crystal, 32_kHz.pin1
  N8: IC4.X2_-_Crystal, Xtal.pin1

notes:
  *
